// Digital circuit ALU.dig as structural Verilog
module ALU (
  input  rst,
  input  clk,
  input  [1:0] op,
  input  [15:0] INBUS,
  input  BEGIN,
  output [15:0] OUTBUS,
  output [2:0] cnt_2_0__mul,
  output [2:0] cnt_2_0__div
);

  wire A_7, A_lsb, add, and_1_out, and_2_out, block_shift, c0, c1, c2, c3, c4, c5, c6, c7, c8, c8_wait, c9,
       c10, c11, c12, c13, c14, c15, c16, c17, c18, cnt_booth, cnt_division, div, END, ld_A,
       ld_duma_scad_division, ld_suma_scad_booth, mul, multiplexer_1_out, multiplexer_3_out, not_1_out,
       not_2_out, notconnected_1_out, or_2_out, or_4_out, or_7_out, or_8_out, or_9_out, or_10_out, or_11_out,
       or_12_out, or_13_out, Q_0, Q__1, sub;
  wire [2:0] or_1_out;
  wire [7:0] multiplexer_2_out, multiplexer_5_out, notconnected_2_out, notconnected_3_out, O_add_sub, O_div,
       O_mul, out_A, out_M, out_Q;

  Multiplexer #(.Selector_Bits(2)) multiplexer_1 (
    .sel({div, mul}), .in_0(1'b0), .in_1(cnt_booth), .in_2(cnt_division), .in_3(notconnected_1_out),
    .out(multiplexer_1_out));
  // NotConnected on notconnected_1_out
  Decoder #(.Selector_Bits(2)) decoder_1 (.sel(op), .out_0(add), .out_1(sub), .out_2(mul), .out_3(div));
  Control_Unit_ALU control_unit_alu_1 (
    .clk(clk), .rst(rst), .BEGIN(BEGIN), .Op(op), .count7(multiplexer_1_out), .a_7(A_7),
    .Q_0_Q__1({Q_0, Q__1}), .END(END), .c0(c0), .c1(c1), .c2(c2), .c3(c3), .c4(c4), .c5(c5), .c6(c6),
    .c7(c7), .c8(c8), .c9(c9), .c10(c10), .c11(c11), .c12(c12), .c13(c13), .c14(c14), .c15(c15), .c16(c16),
    .c17(c17), .c18(c18), .c8_wait(c8_wait));
  or or_1 (or_1_out[0], c2, or_2_out, ld_suma_scad_booth);
  or or_2 (or_2_out, c5, c6);
  Multiplexer #(.Selector_Bits(3), .Bits(8)) multiplexer_2 (
    .sel(or_1_out), .in_0(INBUS[7:0]), .in_1({8{1'b0}}), .in_2(INBUS[15:8]), .in_3(O_add_sub), .in_4(O_mul),
    .in_5(O_div), .in_6(notconnected_2_out), .in_7(notconnected_3_out), .out(multiplexer_2_out));
  // NotConnected on notconnected_2_out
  // NotConnected on notconnected_3_out
  or or_3 (or_1_out[1], c3, or_4_out);
  or or_4 (or_4_out, c5, c6);
  and and_1 (and_1_out, mul, c2);
  or or_5 (or_1_out[2], ld_suma_scad_booth, ld_duma_scad_division);
  or or_6 (ld_A, or_7_out, or_10_out, or_11_out);
  or or_7 (or_7_out, c3, c2, c1);
  or or_8 (or_8_out, not_1_out, c6);
  not not_1 (not_1_out, c5);
  or or_9 (or_9_out, and_1_out, rst);
  and and_2 (and_2_out, div, c2);
  or or_10 (or_10_out, c5, c6);
  shift_reg_bidir A (
    .IN(multiplexer_2_out), .load(ld_A), .dr(or_13_out), .clk(clk), .rst(rst), .en(block_shift), .msb(A_7),
    .lsb(A_lsb), .O(out_A));
  or or_11 (or_11_out, ld_suma_scad_booth, ld_duma_scad_division);
  // RCA_SUBTRACTOR rca_subtractor_1: pin names not known; wires that end beside it: out_A, or_8_out, out_M, O_add_sub
  booth_radix_2 booth_radix_2_1 (
    .c9(c9), .c10(c10), .inA(out_A), .inM(out_M), .c12(c12), .rst(or_9_out), .clk(clk), .rca_o(O_mul),
    .ldA(ld_suma_scad_booth), .cnt7(cnt_booth), .cnt_2_0(cnt_2_0__mul));
  restoring_div restoring_div_1 (
    .c16(c16), .c17(c17), .c18(c18), .c12(c12), .rca_div_x(out_A), .rca_div_y(out_M), .rst(and_2_out),
    .clk(clk), .ldAdiv(ld_duma_scad_division), .rca_div_o(O_div), .cnt7(cnt_division), .cnt_2_0(cnt_2_0__div));
  or or_12 (or_12_out, c8, c3);
  or or_13 (or_13_out, not_2_out, div);
  not not_2 (not_2_out, mul);
  Q_shift_reg Q (
    .IN(INBUS[7:0]), .load(or_12_out), .dr(or_13_out), .clk(clk), .rst(rst), .en(block_shift), .a0(A_lsb),
    .a7(c13), .c13(c16), .c16(A_7), .lsb(Q_0), .O(out_Q));  // open: msb
  Multiplexer multiplexer_3 (.sel(c8), .in_0(Q_0), .in_1(1'b0), .out(multiplexer_3_out));
  Multiplexer #(.Selector_Bits(2), .Bits(16)) multiplexer_4 (
    .sel({c14, c13}), .in_0({{8{1'b0}}, out_A}), .in_1({{8{1'b0}}, out_Q}), .in_2({out_A, out_Q}),
    .in_3({16{1'b0}}), .out(OUTBUS));
  D_FLIPFLOP d_flipflop_1 (.D(multiplexer_3_out), .CLK(clk), .RST(rst), .Q(Q__1));  // open: Q_neg
  or or_14 (block_shift, c11, ld_A, c15, c8);
  Multiplexer #(.Bits(8)) multiplexer_5 (.sel(rst), .in_0(INBUS[7:0]), .in_1({8{1'b0}}), .out(multiplexer_5_out));
  Register #(.Bits(8)) M (.D(multiplexer_5_out), .C(clk), .en(c4), .Q(out_M));

  // Other names for the same wires on the sheet: INBUS_7_0[7:0] = INBUS[7:0]; INBUS_15_8[7:0] = INBUS[15:8]

  // Notes on the sheet:
  //   dec2:4
endmodule
