// Digital circuit COUNTER.dig as structural Verilog
module COUNTER (
  input  rst,
  input  clk,
  input  EN,
  output count7,
  output [2:0] cnt_2_0
);

  wire ct_nxt_0, ct_nxt_1, ct_nxt_2, multiplexer_1_out, multiplexer_2_out, multiplexer_3_out;

  Multiplexer multiplexer_1 (.sel(EN), .in_0(cnt_2_0[2]), .in_1(ct_nxt_2), .out(multiplexer_1_out));
  D_FLIPFLOP CNT_2 ();
  Add #(.Bits(3)) add_1 (.a(cnt_2_0), .b(3'b001), .c_i(1'b0), .s({ct_nxt_2, ct_nxt_1, ct_nxt_0}));  // open: c_o
  D_FLIPFLOP CNT_1 ();
  Multiplexer multiplexer_2 (.sel(EN), .in_0(cnt_2_0[1]), .in_1(ct_nxt_1), .out(multiplexer_2_out));
  and and_1 (count7, cnt_2_0[0], cnt_2_0[1], cnt_2_0[2]);
  D_FLIPFLOP CNT_0 ();
  Multiplexer multiplexer_3 (.sel(EN), .in_0(cnt_2_0[0]), .in_1(ct_nxt_0), .out(multiplexer_3_out));

  // Notes on the sheet:
  //   clk: Hz: 2147483647
endmodule
