// Digital circuit Control_Unit_ALU.dig as structural Verilog
module Control_Unit_ALU (
  input  clk,
  input  rst,
  input  BEGIN,
  input  [1:0] Op,
  input  count7,
  input  a_7,
  input  [1:0] Q_0_Q__1,
  output END,
  output c0,
  output c1,
  output c2,
  output c3,
  output c4,
  output c5,
  output c6,
  output c7,
  output c8,
  output c9,
  output c10,
  output c11,
  output c12,
  output c13,
  output c14,
  output c15,
  output c16,
  output c17,
  output c18,
  output c8_wait
);

  wire _00, _01, _10, _11, add, and_1_out, and_2_out, and_3_out, and_4_out, and_5_out, and_6_out, and_7_out,
       and_8_out, and_9_out, and_10_out, and_11_out, and_12_out, and_13_out, and_14_out, and_15_out,
       and_16_out, and_17_out, and_18_out, and_19_out, and_20_out, and_21_out, and_22_out, and_23_out,
       and_24_out, and_25_out, and_26_out, and_27_out, and_28_out, and_29_out, div, mul, not_1_out,
       not_2_out, not_3_out, not_4_out, not_5_out, not_6_out, not_7_out, not_8_out, or_1_out, or_2_out,
       or_3_out, or_4_out, or_5_out, or_6_out, or_7_out, or_8_out, or_9_out, or_10_out, or_11_out, or_12_out,
       or_13_out, sub;

  and and_1 (and_1_out, count7, a_7, c17);
  D_FLIPFLOP S18 (.D(and_1_out), .CLK(clk), .RST(rst), .Q(c18));  // open: Q_neg
  and and_2 (and_2_out, a_7, c16);
  D_FLIPFLOP S17 (.D(and_2_out), .CLK(clk), .RST(rst), .Q(c17));  // open: Q_neg
  D_FLIPFLOP S16 (.D(c15), .CLK(clk), .RST(rst), .Q(c16));  // open: Q_neg
  and and_3 (and_3_out, div, c12);
  or or_1 (or_1_out, and_4_out, and_3_out);
  D_FLIPFLOP S15 (.D(or_1_out), .CLK(clk), .RST(rst), .Q(c15));  // open: Q_neg
  and and_4 (and_4_out, div, c4);
  and and_5 (and_5_out, mul, c13);
  or or_2 (or_2_out, and_6_out, and_5_out);
  D_FLIPFLOP S14 (.D(or_2_out), .CLK(clk), .RST(rst), .Q(c14));  // open: Q_neg
  and and_6 (and_6_out, div, c7);
  and and_7 (and_7_out, count7, c9);
  D_FLIPFLOP S13 (.D(and_7_out), .CLK(clk), .RST(rst), .Q(c13));  // open: Q_neg
  not not_1 (not_1_out, a_7);
  not not_2 (not_2_out, count7);
  and and_8 (and_8_out, c16, not_1_out, not_2_out);
  not not_3 (not_3_out, count7);
  and and_9 (and_9_out, not_3_out, c17);
  or or_3 (or_3_out, and_9_out, c11, and_8_out);
  D_FLIPFLOP S12 (.D(or_3_out), .CLK(clk), .RST(rst), .Q(c12));  // open: Q_neg
  or or_4 (or_4_out, _11, _00);
  and and_10 (and_10_out, c12, or_4_out);
  or or_5 (or_5_out, and_14_out, and_13_out, and_12_out, and_10_out);
  and and_11 (and_11_out, mul, or_5_out);
  not not_4 (not_4_out, count7);
  and and_12 (and_12_out, c10, not_4_out);
  not not_5 (not_5_out, count7);
  and and_13 (and_13_out, not_5_out, c9);
  D_FLIPFLOP S11 (.D(and_11_out), .CLK(clk), .RST(rst), .Q(c11));  // open: Q_neg
  or or_6 (or_6_out, _11, _00);
  and and_14 (and_14_out, c8_wait, or_6_out);
  and and_15 (and_15_out, _10, c12);
  or or_7 (or_7_out, and_16_out, and_15_out);
  D_FLIPFLOP S10 (.D(or_7_out), .CLK(clk), .RST(rst), .Q(c10));  // open: Q_neg
  and and_16 (and_16_out, _10, c8_wait);
  and and_17 (and_17_out, _01, c12);
  or or_8 (or_8_out, and_18_out, and_17_out);
  D_FLIPFLOP S9 (.D(or_8_out), .CLK(clk), .RST(rst), .Q(c9));  // open: Q_neg
  and and_18 (and_18_out, _01, c8_wait);
  D_FLIPFLOP S8_wait (.D(c8), .CLK(clk), .RST(rst), .Q(c8_wait));  // open: Q_neg
  and and_19 (and_19_out, mul, c4);
  D_FLIPFLOP S8 (.D(and_19_out), .CLK(clk), .RST(rst), .Q(c8));  // open: Q_neg
  not not_6 (not_6_out, a_7);
  and and_20 (and_20_out, c17, count7, not_6_out);
  or or_9 (or_9_out, and_21_out, c5, c6, c18, and_20_out);
  not not_7 (not_7_out, a_7);
  D_FLIPFLOP S7 (.D(or_9_out), .CLK(clk), .RST(rst), .Q(c7));  // open: Q_neg
  and and_21 (and_21_out, c16, not_7_out, count7);
  and and_22 (and_22_out, sub, c4);
  D_FLIPFLOP S6 (.D(and_22_out), .CLK(clk), .RST(rst), .Q(c6));  // open: Q_neg
  and and_23 (and_23_out, add, c4);
  D_FLIPFLOP S5 (.D(and_23_out), .CLK(clk), .RST(rst), .Q(c5));  // open: Q_neg
  or or_10 (or_10_out, c1, c2, c3);
  D_FLIPFLOP S4 (.D(or_10_out), .CLK(clk), .RST(rst), .Q(c4));  // open: Q_neg
  Decoder #(.Selector_Bits(2)) decoder_1 (.sel(Q_0_Q__1), .out_0(_00), .out_1(_01), .out_2(_10), .out_3(_11));
  and and_24 (and_24_out, div, BEGIN, c0);
  D_FLIPFLOP S3 (.D(and_24_out), .CLK(clk), .RST(rst), .Q(c3));  // open: Q_neg
  and and_25 (and_25_out, mul, BEGIN, c0);
  D_FLIPFLOP S2 (.D(and_25_out), .CLK(clk), .RST(rst), .Q(c2));  // open: Q_neg
  or or_11 (or_11_out, add, sub);
  and and_26 (and_26_out, or_11_out, BEGIN, c0);
  D_FLIPFLOP S1 (.D(and_26_out), .CLK(clk), .RST(rst), .Q(c1));  // open: Q_neg
  not not_8 (not_8_out, BEGIN);
  Decoder #(.Selector_Bits(2)) decoder_2 (.sel(Op), .out_0(add), .out_1(sub), .out_2(mul), .out_3(div));
  or or_12 (or_12_out, not_8_out, END);
  D_FLIPFLOP S0 (.D(or_12_out), .CLK(clk), .RST(rst), .Q(c0));  // open: Q_neg
  or or_13 (or_13_out, sub, add);
  and and_27 (and_27_out, or_13_out, c7);
  or or_14 (END, and_29_out, and_28_out, and_27_out);
  and and_28 (and_28_out, mul, c14);
  and and_29 (and_29_out, div, c14);

  // Other names for the same wires on the sheet: b4 = c4; b7 = c7; b8 = c8; b9 = c9; b10 = c10; b11 = c11; b12 = c12;
  //   b14 = c14; b16 = c16; b17 = c17; b18 = c18; cnt7 = count7; msb_a_7 = a_7; Q[1:0] = Q_0_Q__1; s8_wait = c8_wait

  // Notes on the sheet:
  //   B3
  //   B1
  //   B2
  //   dec2:4
  //   B0
endmodule
