// Digital circuit D_FLIPFLOP.dig as structural Verilog
module D_FLIPFLOP (
  input  D,
  input  CLK,
  input  RST,
  output Q,
  output Q_neg
);

  wire and_1_out, nand_1_out, nand_2_out, nand_3_out, nand_4_out, nand_5_out, nand_6_out, not_1_out,
       not_2_out, not_3_out;

  not not_1 (not_1_out, RST);
  not not_2 (not_2_out, CLK);
  and and_1 (and_1_out, D, not_1_out);
  not not_3 (not_3_out, and_1_out);
  nand nand_1 (nand_1_out, not_3_out, not_2_out);
  nand nand_2 (nand_2_out, and_1_out, not_2_out);
  nand nand_3 (nand_3_out, nand_1_out, nand_4_out);
  nand nand_4 (nand_4_out, nand_2_out, nand_3_out);
  nand nand_5 (nand_5_out, nand_3_out, CLK);
  nand nand_6 (nand_6_out, nand_4_out, CLK);
  nand nand_7 (Q, nand_6_out, Q_neg);
  nand nand_8 (Q_neg, nand_5_out, Q);

  // Notes on the sheet:
  //   CLK: Hz: 10
  //   D_rst
  //   R_master
  //   S_master
  //   Qm_feedback
  //   Qm
  //   R_slave
  //   S_slave
endmodule
