// Digital circuit FAC.dig as structural Verilog
module FAC (
  input  xi,
  input  yi,
  input  ci,
  output zi,
  output ci_plus_1
);

  wire and_1_out, and_2_out, and_3_out, xor_2_out;

  or or_1 (ci_plus_1, and_3_out, and_2_out, and_1_out);
  and and_1 (and_1_out, yi, ci);
  and and_2 (and_2_out, xi, ci);
  and and_3 (and_3_out, xi, yi);
  xor xor_1 (zi, xor_2_out, ci);
  xor xor_2 (xor_2_out, xi, yi);
endmodule
