// Digital circuit Q_shift_reg.dig as structural Verilog
module Q_shift_reg (
  input  [7:0] IN,
  input  load,
  input  dr,
  input  clk,
  input  rst,
  input  en,
  input  a0,
  input  a7,
  input  c13,
  input  c16,
  output msb,
  output lsb,
  output [7:0] O
);

  wire multiplexer_1_out, multiplexer_2_out, multiplexer_3_out, multiplexer_4_out, multiplexer_5_out,
       multiplexer_6_out, multiplexer_7_out, multiplexer_8_out, multiplexer_9_out, multiplexer_10_out,
       multiplexer_11_out, multiplexer_12_out, multiplexer_13_out, multiplexer_14_out, multiplexer_15_out,
       multiplexer_16_out, multiplexer_17_out, MUX_SEL0, not_1_out, not_2_out, notconnected_1_out;

  Multiplexer #(.Selector_Bits(2)) multiplexer_1 (
    .sel({load, MUX_SEL0}), .in_0(a0), .in_1(O[6]), .in_2(IN[7]), .in_3(1'b0), .out(multiplexer_1_out));
  Multiplexer multiplexer_2 (.sel(en), .in_0(msb), .in_1(multiplexer_1_out), .out(multiplexer_2_out));
  D_FLIPFLOP FF7 (.D(multiplexer_2_out), .CLK(clk), .RST(rst), .Q(msb));  // open: Q_neg
  Multiplexer #(.Selector_Bits(2)) multiplexer_3 (
    .sel({load, MUX_SEL0}), .in_0(msb), .in_1(O[5]), .in_2(IN[6]), .in_3(1'b0), .out(multiplexer_3_out));
  Multiplexer multiplexer_4 (.sel(en), .in_0(O[6]), .in_1(multiplexer_3_out), .out(multiplexer_4_out));
  D_FLIPFLOP FF6 (.D(multiplexer_4_out), .CLK(clk), .RST(rst), .Q(O[6]));  // open: Q_neg
  Multiplexer #(.Selector_Bits(2)) multiplexer_5 (
    .sel({load, MUX_SEL0}), .in_0(O[6]), .in_1(O[4]), .in_2(IN[5]), .in_3(1'b0), .out(multiplexer_5_out));
  Multiplexer multiplexer_6 (.sel(en), .in_0(O[5]), .in_1(multiplexer_5_out), .out(multiplexer_6_out));
  D_FLIPFLOP FF5 (.D(multiplexer_6_out), .CLK(clk), .RST(rst), .Q(O[5]));  // open: Q_neg
  Multiplexer #(.Selector_Bits(2)) multiplexer_7 (
    .sel({load, MUX_SEL0}), .in_0(O[5]), .in_1(O[3]), .in_2(IN[4]), .in_3(1'b0), .out(multiplexer_7_out));
  Multiplexer multiplexer_8 (.sel(en), .in_0(O[4]), .in_1(multiplexer_7_out), .out(multiplexer_8_out));
  D_FLIPFLOP FF4 (.D(multiplexer_8_out), .CLK(clk), .RST(rst), .Q(O[4]));  // open: Q_neg
  Multiplexer #(.Selector_Bits(2)) multiplexer_9 (
    .sel({load, MUX_SEL0}), .in_0(O[4]), .in_1(O[2]), .in_2(IN[3]), .in_3(1'b0), .out(multiplexer_9_out));
  Multiplexer multiplexer_10 (.sel(en), .in_0(O[3]), .in_1(multiplexer_9_out), .out(multiplexer_10_out));
  D_FLIPFLOP FF3 (.D(multiplexer_10_out), .CLK(clk), .RST(rst), .Q(O[3]));  // open: Q_neg
  Multiplexer #(.Selector_Bits(2)) multiplexer_11 (
    .sel({load, MUX_SEL0}), .in_0(O[3]), .in_1(O[1]), .in_2(IN[2]), .in_3(1'b0), .out(multiplexer_11_out));
  and and_1 (MUX_SEL0, not_1_out, dr);
  not not_1 (not_1_out, load);
  Multiplexer multiplexer_12 (.sel(en), .in_0(O[2]), .in_1(multiplexer_11_out), .out(multiplexer_12_out));
  D_FLIPFLOP FF2 (.D(multiplexer_12_out), .CLK(clk), .RST(rst), .Q(O[2]));  // open: Q_neg
  Multiplexer #(.Selector_Bits(2)) multiplexer_13 (
    .sel({load, MUX_SEL0}), .in_0(O[2]), .in_1(lsb), .in_2(IN[1]), .in_3(1'b0), .out(multiplexer_13_out));
  Multiplexer multiplexer_14 (.sel(en), .in_0(O[1]), .in_1(multiplexer_13_out), .out(multiplexer_14_out));
  not not_2 (not_2_out, a7);
  D_FLIPFLOP FF1 (.D(multiplexer_14_out), .CLK(clk), .RST(rst), .Q(O[1]));  // open: Q_neg
  Multiplexer #(.Selector_Bits(2)) multiplexer_15 (
    .sel({c16, c13}), .in_0(O[1]), .in_1(1'b0), .in_2(not_2_out), .in_3(notconnected_1_out),
    .out(multiplexer_15_out));
  // NotConnected on notconnected_1_out
  Multiplexer #(.Selector_Bits(2)) multiplexer_16 (
    .sel({load, MUX_SEL0}), .in_0(multiplexer_15_out), .in_1(1'b0), .in_2(IN[0]), .in_3(1'b0),
    .out(multiplexer_16_out));
  Multiplexer multiplexer_17 (.sel(en), .in_0(lsb), .in_1(multiplexer_16_out), .out(multiplexer_17_out));
  D_FLIPFLOP FF0 (.D(multiplexer_17_out), .CLK(clk), .RST(rst), .Q(lsb));  // open: Q_neg

  assign {O[7], O[0]} = {msb, lsb};

  // Other names for the same wires on the sheet: dir = dr; b0 = IN[0]; b1 = IN[1]; b2 = IN[2]; b3 = IN[3]; b4 = IN[4];
  //   b5 = IN[5]; b6 = IN[6]; b7 = IN[7]; ld = load
endmodule
