// Digital circuit RCA_SUBTRACTOR.dig as structural Verilog
module RCA_SUBTRACTOR (
  input  [7:0] X,
  input  [1:0] OP,
  input  [7:0] Y,
  output [7:0] Z,
  output c_out
);

  wire xor_1_out, xor_2_out, xor_3_out, xor_4_out, xor_5_out, xor_6_out, xor_7_out, xor_8_out;

  FAC FAC7 ();
  FAC FAC6 ();
  FAC FAC5 ();
  xor xor_1 (xor_1_out, OP[0], Y[7]);
  xor xor_2 (xor_2_out, OP[0], Y[6]);
  FAC FAC4 ();
  xor xor_3 (xor_3_out, OP[0], Y[5]);
  xor xor_4 (xor_4_out, OP[0], Y[4]);
  FAC FAC3 ();
  xor xor_5 (xor_5_out, OP[0], Y[3]);
  xor xor_6 (xor_6_out, OP[0], Y[2]);
  FAC FAC2 ();
  xor xor_7 (xor_7_out, OP[0], Y[1]);
  FAC FAC1 ();
  xor xor_8 (xor_8_out, OP[0], Y[0]);
  FAC FAC0 ();
  // Pins of 1 and 2 bits meet at OP
endmodule
