// Digital circuit booth_radix_2.dig as structural Verilog
module booth_radix_2 (
  input  c9,
  input  c10,
  input  [7:0] inA,
  input  [7:0] inM,
  input  c12,
  input  rst,
  input  clk,
  output [7:0] rca_o,
  output ldA,
  output cnt7,
  output [2:0] cnt_2_0
);

  wire not_2_out, op;
  wire [7:0] add_1_s, multiplexer_1_out, not_1_out;

  COUNTER counter_1 (.rst(rst), .clk(clk), .EN(c12), .count7(cnt7), .cnt_2_0(cnt_2_0));
  assign not_1_out = ~inM;  // Not not_1, 8 bits wide
  Add #(.Bits(8)) add_1 (.a(not_1_out), .b(8'h1), .c_i(1'b0), .s(add_1_s));  // open: c_o
  Multiplexer #(.Bits(8)) multiplexer_1 (.sel(c10), .in_0(inM), .in_1(add_1_s), .out(multiplexer_1_out));
  // RCA_SUBTRACTOR rca_subtractor_1: pin names not known; wires that end beside it: inA, 1'b0, multiplexer_1_out, rca_o
  and and_1 (op, not_2_out, c10);
  not not_2 (not_2_out, c9);
  or or_1 (ldA, c9, c10);
endmodule
