// Digital circuit restoring_div.dig as structural Verilog
module restoring_div (
  input  c16,
  input  c17,
  input  c18,
  input  c12,
  input  [7:0] rca_div_x,
  input  [7:0] rca_div_y,
  input  rst,
  input  clk,
  output ldAdiv,
  output [7:0] rca_div_o,
  output cnt7,
  output [2:0] cnt_2_0
);

  wire not_1_out, not_2_out, op;

  not not_1 (not_1_out, c17);
  not not_2 (not_2_out, c18);
  and and_1 (op, c16, not_1_out, not_2_out);
  // RCA_SUBTRACTOR rca_subtractor_1: pin names not known; wires that end beside it: rca_div_x, op, rca_div_y, rca_div_o
  COUNTER counter_1 (.rst(rst), .clk(clk), .EN(c12), .count7(cnt7), .cnt_2_0(cnt_2_0));
  or or_1 (ldAdiv, c16, c17, c18);
endmodule
